// Logisim project Calc.circ as structural Verilog: 7 circuits, main circuit main
module main (
  input  in_1,
  input  in_2,
  input  in_3,
  input  in_4,
  input  in_5,
  input  in_6,
  input  in_7,
  input  in_8
);

  wire additionneur_4_bits_1_out_10, additionneur_4_bits_1_out_11, additionneur_4_bits_1_out_12,
       additionneur_4_bits_1_out_13, additionneur_4_bits_1_retenue, retenue_1_retenue, retenue_2_retenue,
       tabresult_1_a_2, tabresult_1_b_2, tabresult_1_c_2, tabresult_1_d_2, tabresult_1_e, tabresult_1_f,
       tabresult_1_g, tabresult_2_a_2, tabresult_2_b_2, tabresult_2_c_2, tabresult_2_d_2, tabresult_2_e,
       tabresult_2_f, tabresult_2_g, tabresult_3_a_2, tabresult_3_b_2, tabresult_3_c_2, tabresult_3_d_2,
       tabresult_3_e, tabresult_3_f, tabresult_3_g, tabresult_4_a_2, tabresult_4_b_2, tabresult_4_c_2,
       tabresult_4_d_2, tabresult_4_e, tabresult_4_f, tabresult_4_g, tabresult_5_a_2, tabresult_5_b_2,
       tabresult_5_c_2, tabresult_5_d_2, tabresult_5_e, tabresult_5_f, tabresult_5_g;

  tabResult tabresult_1 (
    .D(in_1), .C(in_3), .B(in_5), .A(in_7), .a_2(tabresult_1_a_2), .b_2(tabresult_1_b_2),
    .c_2(tabresult_1_c_2), .d_2(tabresult_1_d_2), .e(tabresult_1_e), .f(tabresult_1_f), .g(tabresult_1_g));
  Retenue retenue_1 (.D(in_1), .C(in_3), .B(in_5), .A(in_7), .retenue(retenue_1_retenue));
  _7_Segment_Display u_7_segment_display_1 (
    .g(tabresult_1_g), .f(tabresult_1_f), .a(tabresult_1_a_2), .b(tabresult_1_b_2), .e(tabresult_1_e),
    .d(tabresult_1_d_2), .c(tabresult_1_c_2), .dp(retenue_1_retenue));
  Button button_1 ();  // open: out
  tabResult tabresult_2 (
    .a_2(tabresult_2_a_2), .b_2(tabresult_2_b_2), .c_2(tabresult_2_c_2), .d_2(tabresult_2_d_2),
    .e(tabresult_2_e), .f(tabresult_2_f), .g(tabresult_2_g));  // open: D, C, B, A
  tabResult tabresult_3 (
    .a_2(tabresult_3_a_2), .b_2(tabresult_3_b_2), .c_2(tabresult_3_c_2), .d_2(tabresult_3_d_2),
    .e(tabresult_3_e), .f(tabresult_3_f), .g(tabresult_3_g));  // open: D, C, B, A
  tabResult tabresult_4 (
    .D(in_2), .C(in_4), .B(in_6), .A(in_8), .a_2(tabresult_4_a_2), .b_2(tabresult_4_b_2),
    .c_2(tabresult_4_c_2), .d_2(tabresult_4_d_2), .e(tabresult_4_e), .f(tabresult_4_f), .g(tabresult_4_g));
  Retenue retenue_2 (.D(in_2), .C(in_4), .B(in_6), .A(in_8), .retenue(retenue_2_retenue));
  Additionneur_4_bits additionneur_4_bits_1 (
    .in_1(in_2), .in_2(in_1), .in_3(in_4), .in_4(in_3), .in_5(in_6), .in_6(in_5), .in_7(in_8), .in_8(in_7),
    .Retenue(additionneur_4_bits_1_retenue), .out_10(additionneur_4_bits_1_out_10),
    .out_11(additionneur_4_bits_1_out_11), .out_12(additionneur_4_bits_1_out_12),
    .out_13(additionneur_4_bits_1_out_13));
  tabResult tabresult_5 (
    .D(additionneur_4_bits_1_out_10), .C(additionneur_4_bits_1_out_11), .B(additionneur_4_bits_1_out_12),
    .A(additionneur_4_bits_1_out_13), .a_2(tabresult_5_a_2), .b_2(tabresult_5_b_2), .c_2(tabresult_5_c_2),
    .d_2(tabresult_5_d_2), .e(tabresult_5_e), .f(tabresult_5_f), .g(tabresult_5_g));
  _7_Segment_Display u_7_segment_display_2 (
    .g(tabresult_3_g), .f(tabresult_3_f), .a(tabresult_3_a_2), .b(tabresult_3_b_2), .e(tabresult_3_e),
    .d(tabresult_3_d_2), .c(tabresult_3_c_2));  // open: dp
  _7_Segment_Display u_7_segment_display_3 (
    .g(tabresult_4_g), .f(tabresult_4_f), .a(tabresult_4_a_2), .b(tabresult_4_b_2), .e(tabresult_4_e),
    .d(tabresult_4_d_2), .c(tabresult_4_c_2), .dp(retenue_2_retenue));
  _7_Segment_Display u_7_segment_display_4 (
    .g(tabresult_2_g), .f(tabresult_2_f), .a(tabresult_2_a_2), .b(tabresult_2_b_2), .e(tabresult_2_e),
    .d(tabresult_2_d_2), .c(tabresult_2_c_2));  // open: dp
  LED led_1 (.in(additionneur_4_bits_1_retenue));
  _7_Segment_Display u_7_segment_display_5 (
    .g(tabresult_5_g), .f(tabresult_5_f), .a(tabresult_5_a_2), .b(tabresult_5_b_2), .e(tabresult_5_e),
    .d(tabresult_5_d_2), .c(tabresult_5_c_2));  // open: dp

  // Notes on the sheet:
  //   tabResult
  //   Retenue
  //   tabResult
  //   Retenue
  //   Retenue
endmodule

module tabResult (
  input  D,
  input  C,
  input  B,
  input  A,
  output a_2,
  output b_2,
  output c_2,
  output d_2,
  output e,
  output f,
  output g
);

  wire and_1_out, and_2_out, and_3_out, and_4_out, and_5_out, and_6_out, and_7_out, and_8_out, and_9_out,
       and_10_out, and_11_out, and_12_out, and_13_out, and_14_out, and_15_out, and_16_out, and_17_out,
       and_18_out, and_19_out, and_20_out, and_21_out, and_22_out, and_23_out, and_24_out, and_25_out,
       and_26_out, not_1_out, not_2_out, not_3_out, not_4_out, not_5_out, not_6_out, not_7_out, not_8_out,
       not_9_out, not_10_out, not_11_out, not_12_out, not_13_out, not_14_out, not_15_out, not_16_out,
       not_17_out, not_18_out, not_19_out, not_20_out, not_21_out, not_22_out, not_23_out, not_24_out,
       not_25_out, not_26_out, not_27_out, not_28_out, not_29_out, or_1_out, or_2_out, or_3_out, or_4_out,
       or_5_out, or_6_out, or_7_out, or_8_out, or_9_out, or_10_out, or_12_out, or_13_out, or_15_out,
       or_16_out;

  not not_1 (not_1_out, C);
  and and_1 (and_1_out, not_1_out, not_2_out);
  not not_2 (not_2_out, A);
  and and_2 (and_2_out, C, A);
  not not_3 (not_3_out, D);
  not not_4 (not_4_out, C);
  not not_5 (not_5_out, D);
  and and_3 (and_3_out, not_5_out, not_6_out);
  not not_6 (not_6_out, B);
  not not_7 (not_7_out, A);
  not not_8 (not_8_out, C);
  not not_9 (not_9_out, B);
  not not_10 (not_10_out, D);
  and and_4 (and_4_out, not_10_out, B);
  not not_11 (not_11_out, C);
  and and_5 (and_5_out, not_11_out, not_12_out);
  not not_12 (not_12_out, B);
  not not_13 (not_13_out, D);
  and and_6 (and_6_out, not_13_out, A);
  not not_14 (not_14_out, D);
  not not_15 (not_15_out, C);
  and and_7 (and_7_out, not_15_out, not_16_out);
  not not_16 (not_16_out, A);
  not not_17 (not_17_out, C);
  and and_8 (and_8_out, not_17_out, B);
  not not_18 (not_18_out, A);
  and and_9 (and_9_out, C, not_19_out);
  not not_19 (not_19_out, B);
  not not_20 (not_20_out, C);
  and and_10 (and_10_out, not_20_out, not_21_out);
  not not_21 (not_21_out, A);
  and and_11 (and_11_out, B, not_22_out);
  not not_22 (not_22_out, A);
  and and_12 (and_12_out, D, B);
  and and_13 (and_13_out, D, C);
  not not_23 (not_23_out, B);
  and and_14 (and_14_out, not_23_out, not_24_out);
  not not_24 (not_24_out, A);
  and and_15 (and_15_out, C, not_25_out);
  not not_25 (not_25_out, B);
  and and_16 (and_16_out, C, not_26_out);
  not not_26 (not_26_out, A);
  not not_27 (not_27_out, C);
  and and_17 (and_17_out, not_27_out, B);
  and and_18 (and_18_out, C, not_28_out);
  not not_28 (not_28_out, B);
  and and_19 (and_19_out, C, not_29_out);
  not not_29 (not_29_out, A);
  or or_1 (or_1_out, and_1_out, B);
  or or_2 (or_2_out, and_2_out, D);
  and and_20 (and_20_out, not_3_out, not_4_out);
  and and_21 (and_21_out, and_3_out, not_7_out);
  and and_22 (and_22_out, not_8_out, not_9_out);
  and and_23 (and_23_out, and_4_out, A);
  or or_3 (or_3_out, and_5_out, and_6_out);
  and and_24 (and_24_out, not_14_out, C);
  or or_4 (or_4_out, and_7_out, and_8_out);
  and and_25 (and_25_out, B, not_18_out);
  and and_26 (and_26_out, and_9_out, A);
  or or_5 (or_5_out, and_10_out, and_11_out);
  or or_6 (or_6_out, and_12_out, and_13_out);
  or or_7 (or_7_out, and_14_out, and_15_out);
  or or_8 (or_8_out, and_16_out, D);
  or or_9 (or_9_out, and_17_out, and_18_out);
  or or_10 (or_10_out, and_19_out, D);
  or or_11 (a_2, or_1_out, or_2_out);
  or or_12 (or_12_out, and_20_out, and_21_out);
  or or_13 (or_13_out, and_22_out, and_23_out);
  or or_14 (c_2, or_3_out, and_24_out);
  or or_15 (or_15_out, or_4_out, and_25_out);
  or or_16 (or_16_out, and_26_out, D);
  or or_17 (e, or_5_out, or_6_out);
  or or_18 (f, or_7_out, or_8_out);
  or or_19 (g, or_9_out, or_10_out);
  or or_20 (b_2, or_12_out, or_13_out);
  or or_21 (d_2, or_15_out, or_16_out);
endmodule

module Retenue (
  input  D,
  input  C,
  input  B,
  input  A,
  output retenue
);

  wire and_1_out, and_2_out;

  and and_1 (and_1_out, D, B);
  and and_2 (and_2_out, D, C);
  or or_1 (retenue, and_1_out, and_2_out);
endmodule

module _1_2_Additionneur (
  input  in_1,
  input  in_2,
  output Sortie,
  output Retenue
);

  xor xor_1 (Sortie, in_1, in_2);
  and and_1 (Retenue, in_1, in_2);
endmodule

module Additionneur (
  input  R,
  input  A,
  input  B,
  output Resultat,
  output Retenue
);

  wire n1_2_additionneur_1_retenue, n1_2_additionneur_1_sortie, n1_2_additionneur_2_retenue;

  _1_2_Additionneur u_1_2_additionneur_1 (
    .in_1(A), .in_2(B), .Sortie(n1_2_additionneur_1_sortie), .Retenue(n1_2_additionneur_1_retenue));
  _1_2_Additionneur u_1_2_additionneur_2 (
    .in_1(R), .in_2(n1_2_additionneur_1_sortie), .Sortie(Resultat), .Retenue(n1_2_additionneur_2_retenue));
  or or_1 (Retenue, n1_2_additionneur_2_retenue, n1_2_additionneur_1_retenue);
endmodule

module Additionneur_4_bits (
  input  in_1,
  input  in_2,
  input  in_3,
  input  in_4,
  input  in_5,
  input  in_6,
  input  in_7,
  input  in_8,
  output Retenue,
  output out_10,
  output out_11,
  output out_12,
  output out_13
);

  wire additionneur_2_retenue, additionneur_3_retenue, additionneur_4_retenue, not_1_out;

  not not_1 (not_1_out, 1'b1);
  Additionneur additionneur_1 (.R(additionneur_2_retenue), .A(in_2), .B(in_1), .Resultat(out_10), .Retenue(Retenue));
  Additionneur additionneur_2 (
    .R(additionneur_3_retenue), .A(in_4), .B(in_3), .Resultat(out_11), .Retenue(additionneur_2_retenue));
  Additionneur additionneur_3 (
    .R(additionneur_4_retenue), .A(in_6), .B(in_5), .Resultat(out_12), .Retenue(additionneur_3_retenue));
  Additionneur additionneur_4 (.R(not_1_out), .A(in_8), .B(in_7), .Resultat(out_13), .Retenue(additionneur_4_retenue));

  // Notes on the sheet:
  //   Resultat
endmodule

module Test_afficheur_en_ligne (
);

  wire _1_a_2, _1_b_2, _1_c_2, _1_d_2, _1_e, _1_f, _1_g, _2_a_2, _2_b_2, _2_c_2, _2_d_2, _2_e, _2_f, _2_g,
       _3_a_2, _3_b_2, _3_c_2, _3_d_2, _3_e, _3_f, _3_g, _4_a_2, _4_b_2, _4_c_2, _4_d_2, _4_e, _4_f, _4_g;

  tabResult _2 (
    .a_2(_2_a_2), .b_2(_2_b_2), .c_2(_2_c_2), .d_2(_2_d_2), .e(_2_e), .f(_2_f), .g(_2_g));  // open: D, C, B, A
  tabResult _1 (
    .a_2(_1_a_2), .b_2(_1_b_2), .c_2(_1_c_2), .d_2(_1_d_2), .e(_1_e), .f(_1_f), .g(_1_g));  // open: D, C, B, A
  tabResult _3 (
    .a_2(_3_a_2), .b_2(_3_b_2), .c_2(_3_c_2), .d_2(_3_d_2), .e(_3_e), .f(_3_f), .g(_3_g));  // open: D, C, B, A
  tabResult _4 (
    .a_2(_4_a_2), .b_2(_4_b_2), .c_2(_4_c_2), .d_2(_4_d_2), .e(_4_e), .f(_4_f), .g(_4_g));  // open: D, C, B, A
  // NOT_Gate not_1 is placed but not wired
  _7_Segment_Display u_7_segment_display_1 (
    .g(_1_g), .f(_1_f), .a(_1_a_2), .b(_1_b_2), .e(_1_e), .d(_1_d_2), .c(_1_c_2));  // open: dp
  _7_Segment_Display u_7_segment_display_2 (
    .g(_3_g), .f(_3_f), .a(_3_a_2), .b(_3_b_2), .e(_3_e), .d(_3_d_2), .c(_3_c_2));  // open: dp
  _7_Segment_Display u_7_segment_display_3 (
    .g(_2_g), .f(_2_f), .a(_2_a_2), .b(_2_b_2), .e(_2_e), .d(_2_d_2), .c(_2_c_2));  // open: dp
  _7_Segment_Display u_7_segment_display_4 (
    .g(_4_g), .f(_4_f), .a(_4_a_2), .b(_4_b_2), .e(_4_e), .d(_4_d_2), .c(_4_c_2));  // open: dp
endmodule
