// Logisim project les_10_chiffres.circ as structural Verilog: 9 circuits, main circuit main
module main (
  input  in_1,
  input  in_2,
  input  in_3,
  input  in_4,
  input  in_5,
  input  in_6,
  input  in_7,
  input  in_8
);

  wire add4bit_1_sorite_3, add4bit_1_sortie_0, add4bit_1_sortie_1, add4bit_1_sortie_2, afficheur7segs_1_a,
       afficheur7segs_1_b, afficheur7segs_1_c, afficheur7segs_1_d, afficheur7segs_1_e, afficheur7segs_1_f,
       afficheur7segs_1_g, afficheur7segs_2_a, afficheur7segs_2_b, afficheur7segs_2_c, afficheur7segs_2_d,
       afficheur7segs_2_e, afficheur7segs_2_f, afficheur7segs_2_g, afficheur7segs_3_a, afficheur7segs_3_b,
       afficheur7segs_3_c, afficheur7segs_3_d, afficheur7segs_3_e, afficheur7segs_3_f, afficheur7segs_3_g,
       afficheur7segs_4_a, afficheur7segs_4_b, afficheur7segs_4_c, afficheur7segs_4_d, afficheur7segs_4_e,
       afficheur7segs_4_f, afficheur7segs_4_g, retenue_1_retenue, retenue_2_retenue, sous4bit_1_sorite_3,
       sous4bit_1_sortie_0, sous4bit_1_sortie_1, sous4bit_1_sortie_2;

  afficheur7segs afficheur7segs_1 (
    .b4(in_1), .b3(in_3), .b2(in_5), .b1(in_7), .a(afficheur7segs_1_a), .b(afficheur7segs_1_b),
    .c(afficheur7segs_1_c), .d(afficheur7segs_1_d), .e(afficheur7segs_1_e), .f(afficheur7segs_1_f),
    .g(afficheur7segs_1_g));
  retenue retenue_1 (.b4(in_1), .b3(in_3), .b2(in_5), .b1(in_7), .retenue(retenue_1_retenue));
  LED led_1 (.in(retenue_1_retenue));
  _7_Segment_Display u_7_segment_display_1 (
    .g(afficheur7segs_1_g), .f(afficheur7segs_1_f), .a(afficheur7segs_1_a), .b(afficheur7segs_1_b),
    .e(afficheur7segs_1_e), .d(afficheur7segs_1_d), .c(afficheur7segs_1_c));  // open: dp
  retenue retenue_2 (.b4(in_2), .b3(in_4), .b2(in_6), .b1(in_8), .retenue(retenue_2_retenue));
  add4bit add4bit_1 (
    .bit_3(in_2), .A3(in_1), .bit_2(in_4), .A2(in_3), .bit_1(in_6), .A1(in_5), .bit_0(in_8), .A0(in_7),
    .sorite_3(add4bit_1_sorite_3), .sortie_2(add4bit_1_sortie_2), .sortie_1(add4bit_1_sortie_1),
    .sortie_0(add4bit_1_sortie_0));  // open: dépassement
  sous4bit sous4bit_1 (
    .bit_3(in_2), .A3(in_1), .bit_2(in_4), .A2(in_3), .bit_1(in_6), .A1(in_5), .bit_0(in_8), .A0(in_7),
    .sorite_3(sous4bit_1_sorite_3), .sortie_2(sous4bit_1_sortie_2), .sortie_1(sous4bit_1_sortie_1),
    .sortie_0(sous4bit_1_sortie_0));  // open: dépassement
  afficheur7segs afficheur7segs_2 (
    .b4(in_2), .b3(in_4), .b2(in_6), .b1(in_8), .a(afficheur7segs_2_a), .b(afficheur7segs_2_b),
    .c(afficheur7segs_2_c), .d(afficheur7segs_2_d), .e(afficheur7segs_2_e), .f(afficheur7segs_2_f),
    .g(afficheur7segs_2_g));
  LED led_2 (.in(retenue_2_retenue));
  afficheur7segs afficheur7segs_3 (
    .b4(add4bit_1_sorite_3), .b3(add4bit_1_sortie_2), .b2(add4bit_1_sortie_1), .b1(add4bit_1_sortie_0),
    .a(afficheur7segs_3_a), .b(afficheur7segs_3_b), .c(afficheur7segs_3_c), .d(afficheur7segs_3_d),
    .e(afficheur7segs_3_e), .f(afficheur7segs_3_f), .g(afficheur7segs_3_g));
  _7_Segment_Display u_7_segment_display_2 (
    .g(afficheur7segs_2_g), .f(afficheur7segs_2_f), .a(afficheur7segs_2_a), .b(afficheur7segs_2_b),
    .e(afficheur7segs_2_e), .d(afficheur7segs_2_d), .c(afficheur7segs_2_c));  // open: dp
  afficheur7segs afficheur7segs_4 (
    .b4(sous4bit_1_sorite_3), .b3(sous4bit_1_sortie_2), .b2(sous4bit_1_sortie_1), .b1(sous4bit_1_sortie_0),
    .a(afficheur7segs_4_a), .b(afficheur7segs_4_b), .c(afficheur7segs_4_c), .d(afficheur7segs_4_d),
    .e(afficheur7segs_4_e), .f(afficheur7segs_4_f), .g(afficheur7segs_4_g));
  _7_Segment_Display u_7_segment_display_3 (
    .g(afficheur7segs_3_g), .f(afficheur7segs_3_f), .a(afficheur7segs_3_a), .b(afficheur7segs_3_b),
    .e(afficheur7segs_3_e), .d(afficheur7segs_3_d), .c(afficheur7segs_3_c));  // open: dp
  _7_Segment_Display u_7_segment_display_4 (
    .g(afficheur7segs_4_g), .f(afficheur7segs_4_f), .a(afficheur7segs_4_a), .b(afficheur7segs_4_b),
    .e(afficheur7segs_4_e), .d(afficheur7segs_4_d), .c(afficheur7segs_4_c));  // open: dp
endmodule

module afficheur7segs (
  input  b4,
  input  b3,
  input  b2,
  input  b1,
  output a,
  output b,
  output c,
  output d,
  output e,
  output f,
  output g
);

  wire and_1_out, and_2_out, and_3_out, and_4_out, and_5_out, and_6_out, and_7_out, and_8_out, and_9_out,
       and_10_out, and_11_out, and_12_out, and_13_out, and_14_out, and_15_out, and_16_out, and_17_out,
       and_18_out, and_19_out, and_20_out, and_21_out, and_22_out, and_23_out, and_24_out, and_25_out,
       and_26_out, not_1_out, not_2_out, not_3_out, not_4_out, not_5_out, not_6_out, not_7_out, not_8_out,
       not_9_out, not_10_out, not_11_out, not_12_out, not_13_out, not_14_out, not_15_out, not_16_out,
       not_17_out, not_18_out, not_19_out, not_20_out, not_21_out, not_22_out, not_23_out, not_24_out,
       not_25_out, not_26_out, not_27_out, not_28_out, not_29_out, or_1_out, or_2_out, or_3_out, or_4_out,
       or_5_out, or_6_out, or_7_out, or_8_out, or_9_out, or_10_out, or_12_out, or_13_out, or_15_out,
       or_16_out;

  not not_1 (not_1_out, b3);
  and and_1 (and_1_out, not_1_out, not_2_out);
  not not_2 (not_2_out, b1);
  and and_2 (and_2_out, b3, b1);
  not not_3 (not_3_out, b4);
  not not_4 (not_4_out, b3);
  not not_5 (not_5_out, b4);
  and and_3 (and_3_out, not_5_out, not_6_out);
  not not_6 (not_6_out, b2);
  not not_7 (not_7_out, b1);
  not not_8 (not_8_out, b3);
  not not_9 (not_9_out, b2);
  not not_10 (not_10_out, b4);
  and and_4 (and_4_out, not_10_out, b2);
  not not_11 (not_11_out, b3);
  and and_5 (and_5_out, not_11_out, not_12_out);
  not not_12 (not_12_out, b2);
  not not_13 (not_13_out, b4);
  and and_6 (and_6_out, not_13_out, b1);
  not not_14 (not_14_out, b4);
  not not_15 (not_15_out, b3);
  and and_7 (and_7_out, not_15_out, not_16_out);
  not not_16 (not_16_out, b1);
  not not_17 (not_17_out, b3);
  and and_8 (and_8_out, not_17_out, b2);
  not not_18 (not_18_out, b1);
  and and_9 (and_9_out, b3, not_19_out);
  not not_19 (not_19_out, b2);
  not not_20 (not_20_out, b3);
  and and_10 (and_10_out, not_20_out, not_21_out);
  not not_21 (not_21_out, b1);
  and and_11 (and_11_out, b2, not_22_out);
  not not_22 (not_22_out, b1);
  and and_12 (and_12_out, b4, b2);
  and and_13 (and_13_out, b4, b3);
  not not_23 (not_23_out, b2);
  and and_14 (and_14_out, not_23_out, not_24_out);
  not not_24 (not_24_out, b1);
  and and_15 (and_15_out, b3, not_25_out);
  not not_25 (not_25_out, b2);
  and and_16 (and_16_out, b3, not_26_out);
  not not_26 (not_26_out, b1);
  not not_27 (not_27_out, b3);
  and and_17 (and_17_out, not_27_out, b2);
  and and_18 (and_18_out, b3, not_28_out);
  not not_28 (not_28_out, b2);
  and and_19 (and_19_out, b3, not_29_out);
  not not_29 (not_29_out, b1);
  or or_1 (or_1_out, and_1_out, b2);
  or or_2 (or_2_out, and_2_out, b4);
  and and_20 (and_20_out, not_3_out, not_4_out);
  and and_21 (and_21_out, and_3_out, not_7_out);
  and and_22 (and_22_out, not_8_out, not_9_out);
  and and_23 (and_23_out, and_4_out, b1);
  or or_3 (or_3_out, and_5_out, and_6_out);
  and and_24 (and_24_out, not_14_out, b3);
  or or_4 (or_4_out, and_7_out, and_8_out);
  and and_25 (and_25_out, b2, not_18_out);
  and and_26 (and_26_out, and_9_out, b1);
  or or_5 (or_5_out, and_10_out, and_11_out);
  or or_6 (or_6_out, and_12_out, and_13_out);
  or or_7 (or_7_out, and_14_out, and_15_out);
  or or_8 (or_8_out, and_16_out, b4);
  or or_9 (or_9_out, and_17_out, and_18_out);
  or or_10 (or_10_out, and_19_out, b4);
  or or_11 (a, or_1_out, or_2_out);
  or or_12 (or_12_out, and_20_out, and_21_out);
  or or_13 (or_13_out, and_22_out, and_23_out);
  or or_14 (c, or_3_out, and_24_out);
  or or_15 (or_15_out, or_4_out, and_25_out);
  or or_16 (or_16_out, and_26_out, b4);
  or or_17 (e, or_5_out, or_6_out);
  or or_18 (f, or_7_out, or_8_out);
  or or_19 (g, or_9_out, or_10_out);
  or or_20 (b, or_12_out, or_13_out);
  or or_21 (d, or_15_out, or_16_out);
endmodule

module retenue (
  input  b4,
  input  b3,
  input  b2,
  input  b1,
  output retenue
);

  wire and_1_out, and_2_out;

  and and_1 (and_1_out, b4, b2);
  and and_2 (and_2_out, b4, b3);
  or or_1 (retenue, and_1_out, and_2_out);
endmodule

module demiadd (
  input  in_1,
  input  in_2,
  output out_3,
  output out_4
);

  xor xor_1 (out_3, in_1, in_2);
  and and_1 (out_4, in_2, in_1);
endmodule

module additionneur (
  input  in_1,
  input  in_2,
  input  in_3,
  output out_4,
  output out_5
);

  wire demiadd_1_out_4, demiadd_2_out_3, demiadd_2_out_4;

  demiadd demiadd_1 (.in_1(in_1), .in_2(demiadd_2_out_3), .out_3(out_4), .out_4(demiadd_1_out_4));
  demiadd demiadd_2 (.in_1(in_2), .in_2(in_3), .out_3(demiadd_2_out_3), .out_4(demiadd_2_out_4));
  or or_1 (out_5, demiadd_1_out_4, demiadd_2_out_4);
endmodule

module add4bit (
  input  bit_3,
  input  A3,
  input  bit_2,
  input  A2,
  input  bit_1,
  input  A1,
  input  bit_0,
  input  A0,
  output \dépassement ,
  output sorite_3,
  output sortie_2,
  output sortie_1,
  output sortie_0
);

  wire additionneur_2_out_5, additionneur_3_out_5, additionneur_4_out_5, not_1_out;

  additionneur additionneur_1 (
    .in_1(bit_3), .in_2(A3), .in_3(additionneur_2_out_5), .out_4(sorite_3), .out_5(\dépassement ));
  additionneur additionneur_2 (
    .in_1(bit_2), .in_2(A2), .in_3(additionneur_3_out_5), .out_4(sortie_2), .out_5(additionneur_2_out_5));
  additionneur additionneur_3 (
    .in_1(bit_1), .in_2(A1), .in_3(additionneur_4_out_5), .out_4(sortie_1), .out_5(additionneur_3_out_5));
  not not_1 (not_1_out, 1'b1);
  additionneur additionneur_4 (
    .in_1(bit_0), .in_2(A0), .in_3(not_1_out), .out_4(sortie_0), .out_5(additionneur_4_out_5));
endmodule

module demisous (
  input  in_1,
  input  in_2,
  output sortie,
  output retenue
);

  wire not_1_out;

  not not_1 (not_1_out, in_2);
  xor xor_1 (sortie, in_1, in_2);
  and and_1 (retenue, not_1_out, in_1);
endmodule

module soustracteur (
  input  in_1,
  input  in_2,
  input  in_3,
  output sortie,
  output retenue
);

  wire demisous_1_retenue, demisous_1_sortie, demisous_2_retenue;

  demisous demisous_1 (.in_1(in_2), .in_2(in_3), .sortie(demisous_1_sortie), .retenue(demisous_1_retenue));
  demisous demisous_2 (.in_1(in_1), .in_2(demisous_1_sortie), .sortie(sortie), .retenue(demisous_2_retenue));
  or or_1 (retenue, demisous_2_retenue, demisous_1_retenue);
endmodule

module sous4bit (
  input  bit_3,
  input  A3,
  input  bit_2,
  input  A2,
  input  bit_1,
  input  A1,
  input  bit_0,
  input  A0,
  output \dépassement ,
  output sorite_3,
  output sortie_2,
  output sortie_1,
  output sortie_0
);

  wire not_1_out, soustracteur_2_retenue, soustracteur_3_retenue, soustracteur_4_retenue;

  soustracteur soustracteur_1 (
    .in_1(bit_3), .in_2(A3), .in_3(soustracteur_2_retenue), .sortie(sorite_3), .retenue(\dépassement ));
  soustracteur soustracteur_2 (
    .in_1(bit_2), .in_2(A2), .in_3(soustracteur_3_retenue), .sortie(sortie_2),
    .retenue(soustracteur_2_retenue));
  soustracteur soustracteur_3 (
    .in_1(bit_1), .in_2(A1), .in_3(soustracteur_4_retenue), .sortie(sortie_1),
    .retenue(soustracteur_3_retenue));
  not not_1 (not_1_out, 1'b1);
  soustracteur soustracteur_4 (
    .in_1(bit_0), .in_2(A0), .in_3(not_1_out), .sortie(sortie_0), .retenue(soustracteur_4_retenue));
endmodule
